// Logisim project constants.circ as structural Verilog: 1 circuit, main circuit main
module main (
  input  k1,
  input  k2,
  input  k3,
  input  k4,
  output Y1,
  output Y2,
  output Y3,
  output Y4,
  output Y5
);

  and and_1 (Y1, k1, 1'b1);
  or or_1 (Y2, k2, 1'b0);
  xor xor_1 (Y3, k3, 1'b1);
  nor nor_1 (Y4, k4, 1'b0);
  not not_1 (Y5, 1'b0);
endmodule
