// Logisim project floating.circ as structural Verilog: 1 circuit, main circuit main
module main (
  input  A,
  input  B,
  output Y,
  output Z
);

  buf and_1 (Y, A);  // AND_Gate
endmodule
