// Logisim project gate_sizes.circ as structural Verilog: 1 circuit, main circuit main
module main (
  input  A,
  input  B,
  input  C,
  input  D,
  input  E,
  output O1,
  output O2,
  output O3,
  output O4,
  output O5,
  output O6,
  output O7,
  output O8,
  output O9,
  output O10,
  output O11,
  output O12,
  output O13,
  output O14,
  output O15,
  output O16
);

  and and_1 (O1, A, B, C);
  or or_1 (O2, A, B, C, D);
  nand nand_1 (O3, A, B, C, D, E);
  nor nor_1 (O4, A, B, C);
  xor xor_1 (O5, A, B, C, D);
  xnor xnor_1 (O6, A, B, C, D, E);
  and and_2 (O7, A, B);
  or or_2 (O8, A, B, C);
  nand nand_2 (O9, A, B, C, D);
  ExactlyOne xor_2 (.out(O10), .in0(A), .in1(B), .in2(C));
  xnor xnor_2 (O11, A, B);
  and and_3 (O12, A, B, C, D, E, A);
  nor nor_2 (O13, A, B, C, D, E, A, B, C);
  ExactlyOne xor_3 (.out(O14), .in0(A), .in1(B), .in2(C), .in3(D), .in4(E));
  NotExactlyOne xnor_3 (.out(O15), .in0(B), .in1(C), .in2(D));
  or or_3 (O16, D, E);
endmodule
