// Logisim project mux2.circ as structural Verilog: 1 circuit, main circuit main
module main (
  input  S,
  input  D0,
  input  D1,
  output Y
);

  wire and_1_out, and_2_out, not_1_out;

  not not_1 (not_1_out, S);
  and and_1 (and_1_out, not_1_out, D0);
  and and_2 (and_2_out, D1, S);
  or or_1 (Y, and_1_out, and_2_out);
endmodule
