// Logisim project negated_inputs.circ as structural Verilog: 1 circuit, main circuit main
module main (
  input  n1a,
  input  n1b,
  input  n4b,
  input  n4a,
  input  n3a,
  input  n3b,
  input  n3c,
  input  n2a,
  input  n2b,
  input  n2c,
  output N3,
  output N1,
  output N2,
  output N4
);

  and and_1 (N1, ~n1a, n1b);  // AND_Gate
  or or_1 (N2, ~n2a, n2b, n2c);  // OR_Gate
  nand nand_1 (N3, n3a, n3b, ~n3c);  // NAND_Gate
  xor xor_1 (N4, n4a, ~n4b);  // XOR_Gate
endmodule
