// Logisim project rotated.circ as structural Verilog: 1 circuit, main circuit main
module main (
  input  r2a,
  input  r2b,
  input  r2c,
  input  r1a,
  input  r1b,
  input  r5,
  input  r3a,
  input  r6,
  input  r3b,
  input  r4,
  output Q1,
  output Q2,
  output Q4,
  output Q3,
  output Q6,
  output Q5
);

  and and_1 (Q1, r1a, r1b);
  xnor xnor_1 (Q3, r3a, r3b);
  or or_1 (Q2, r2a, r2b, r2c);
  not not_1 (Q4, r4);
  buf buffer_1 (Q5, r5);
  not not_2 (Q6, r6);
endmodule
