// Logisim project unlabelled_pins.circ as structural Verilog: 1 circuit, main circuit main
module main (
  input  in_1,
  input  in_2,
  input  IN1,
  output out_4
);

  and and_1 (out_4, in_1, in_2, IN1);
endmodule
