// Logisim project unsupported.circ as structural Verilog: 2 circuits, main circuit main
module main (
  input  A,
  input  B,
  output Y
);

  and and_1 (Y, A, B);
  // Probe on nothing
  D_Flip_Flop d_ff_1 ();  // open: D, clk, Q, Qn, preset, reset
  Multiplexer multiplexer_1 ();  // open: in0, in1, out, sel
  Clock clock_1 ();  // open: out
  LED led_1 ();  // open: in
  helper helper_1 ();  // open: h

  // Notes on the sheet:
  //   ignored note
endmodule

module helper (
  input  h
);
endmodule
